// Digital circuit 박건호_2023320123.dig as structural Verilog
module \박건호_2023320123  (
  input  input1,
  input  input2,
  input  input_A,
  input  input_B,
  output \output ,
  output output_2
);

  xor xor_1 (\output , input1, input2);
  xor_gate #(.applicationType("IVERILOG")) u_xor_gate (.A(input_A), .B(input_B), .Y(output_2));
  LED led_1 (.in(\output ));
  LED led_2 (.in(output_2));
endmodule

/* Code of xor_gate:
module xor_gate (
	input wire A,
	input wire B,
	output wire Y
);

assign Y = A ^ B;

endmodule
*/
