// Digital circuit 박건호_2023320123.dig as structural Verilog
module \박건호_2023320123  (
  input  D0,
  input  D1,
  input  D2,
  input  D3,
  output Sa,
  output Sb,
  output Sd,
  output Se,
  output Sf,
  output Sg,
  output Sc
);

  segment #(.applicationType("IVERILOG")) u_segment (
    .D0(D0), .D1(D1), .D2(D2), .D3(D3), .Sa(Sa), .Sb(Sb), .Sc(Sc), .Sd(Sd), .Se(Se), .Sf(Sf), .Sg(Sg));
  LED led_1 (.in(Sf));
  LED led_2 (.in(Se));
  LED led_3 (.in(Sa));
  LED led_4 (.in(Sg));
  LED led_5 (.in(Sd));
  LED led_6 (.in(Sb));
  LED led_7 (.in(Sc));
endmodule

/* Code of segment:
module segment (
    input wire D0,
    input wire D1,
    input wire D2,
    input wire D3,
    output wire Sa,
    output wire Sb,
    output wire Sc,
    output wire Sd,
    output wire Se,
    output wire Sf,
    output wire Sg
);

assign Sa = ~D3 & D1 | ~D3 & D2 & D0 | D3 & ~D2 & ~D1 | ~D2 & ~D1 & ~D0;
assign Sb = ~D3 & ~D2 | ~D2 & ~D1 | ~D3 & D1 & D0 | ~D3 & ~D1 & ~D0;
assign Sc = ~D3 & ~D1 | ~D3 & D1 & D0 | D1 & ~D0 & ~D3 & D2 | D3 & ~D2 & ~D1;
assign Sd = ~D2 & ~D0 & ~D1 | ~D3 & D2 & ~D1 & D0 | ~D3 & ~D2 & D1 | ~D3 & D2 & D1 & ~D0;
assign Se = ~D0 & ~D1 & ~D2 | D1 & ~D0 & ~D3;
assign Sf = ~D3 & D2 & ~D1 & D0 | ~D3 & D2 & D1 & ~D0 | ~D0 & ~D1 & ~D3 | ~D1 & D3 & ~D2;
assign Sg = ~D3 & ~D2 & D1 | ~D3 & D2 & D1 & ~D0 | ~D1 & D3 & ~D2 | ~D3 & D2 & ~D1;

endmodule
*/
