// Digital circuit 박건호_2023320123.dig as structural Verilog
module \박건호_2023320123  (
  input  A3,
  input  A2,
  input  A1,
  input  A0,
  output Y3,
  output Y2,
  output Y1,
  output Y0
);

  \priority  #(.applicationType("IVERILOG")) u_priority (
    .A3(A3), .A2(A2), .A1(A1), .A0(A0), .Y3(Y3), .Y2(Y2), .Y1(Y1), .Y0(Y0));
endmodule

/* Code of priority:
module priority (
	input wire A3,
	input wire A2,
	input wire A1,
	input wire A0,
	output wire Y3,
	output wire Y2,
	output wire Y1,
	output wire Y0
);

assign Y3 = A3;
assign Y2 = ~A3 & A2;
assign Y1 = ~A3 & ~A2 & A1;
assign Y0 = ~A3 & ~A2 & ~A1 & A0;

endmodule
*/
