// Digital circuit 박건호_2023320123-last.dig as structural Verilog
module \박건호_2023320123_last  (
  input  Clock_In
);

  wire Down_button_2_out, Down_button_3_out, Reset_out, u_edge_detector_2_q_o, u_edge_detector_3_q_o,
       u_edge_detector_4_q_o, u_edge_detector_q_o, u_elevator_machine_direction1_o,
       u_elevator_machine_direction2_o, u_synchronizer_2_q_o, u_synchronizer_3_q_o, u_synchronizer_4_q_o,
       u_synchronizer_q_o, Up_button_1_out, Up_button_2_out;
  wire [3:0] u_elevator_machine_cur_floor_o;

  Button Up_button_1 (.out(Up_button_1_out));
  Button Up_button_2 (.out(Up_button_2_out));
  Button Down_button_2 (.out(Down_button_2_out));
  Button Down_button_3 (.out(Down_button_3_out));
  synchronizer #(.applicationType("IVERILOG")) u_synchronizer (
    .clk_i(Clock_In), .d_i(Up_button_1_out), .q_o(u_synchronizer_q_o));
  synchronizer #(.applicationType("IVERILOG")) u_synchronizer_2 (
    .clk_i(Clock_In), .d_i(Up_button_2_out), .q_o(u_synchronizer_2_q_o));
  synchronizer #(.applicationType("IVERILOG")) u_synchronizer_3 (
    .clk_i(Clock_In), .d_i(Down_button_2_out), .q_o(u_synchronizer_3_q_o));
  synchronizer #(.applicationType("IVERILOG")) u_synchronizer_4 (
    .clk_i(Clock_In), .d_i(Down_button_3_out), .q_o(u_synchronizer_4_q_o));
  edge_detector #(.applicationType("IVERILOG")) u_edge_detector (
    .clk_i(Clock_In), .d_i(u_synchronizer_q_o), .q_o(u_edge_detector_q_o));
  edge_detector #(.applicationType("IVERILOG")) u_edge_detector_2 (
    .clk_i(Clock_In), .d_i(u_synchronizer_2_q_o), .q_o(u_edge_detector_2_q_o));
  edge_detector #(.applicationType("IVERILOG")) u_edge_detector_3 (
    .clk_i(Clock_In), .d_i(u_synchronizer_3_q_o), .q_o(u_edge_detector_3_q_o));
  edge_detector #(.applicationType("IVERILOG")) u_edge_detector_4 (
    .clk_i(Clock_In), .d_i(u_synchronizer_4_q_o), .q_o(u_edge_detector_4_q_o));
  Button Reset (.out(Reset_out));
  elevator_machine #(.applicationType("IVERILOG")) u_elevator_machine (
    .rst_i(Reset_out), .clk_i(Clock_In), .up_btn_i1(u_edge_detector_q_o), .up_btn_i2(u_edge_detector_2_q_o),
    .down_btn_i2(u_edge_detector_3_q_o), .down_btn_i3(u_edge_detector_4_q_o),
    .cur_floor_o(u_elevator_machine_cur_floor_o), .direction1_o(u_elevator_machine_direction1_o),
    .direction2_o(u_elevator_machine_direction2_o));
  Seven_Seg_Hex seven_seg_hex_1 (.d(u_elevator_machine_cur_floor_o), .dp(1'b0));
  LED led_1 (.in(u_elevator_machine_direction1_o));
  LED led_2 (.in(u_elevator_machine_direction2_o));

  // Notes on the sheet:
  //   Clock_In: Hz: 50000000
endmodule

/* Code of synchronizer:
`timescale 1ns/1ps

module synchronizer (
	 input clk_i
	,input d_i

	,output reg q_o
);


	reg ff1_r;

	always @(posedge clk_i) begin
		ff1_r <= d_i;
		q_o <= ff1_r;
	end

endmodule
*/

/* Code of edge_detector:
`timescale 1ns/1ps

module edge_detector (
	 input clk_i
	,input d_i

	,output q_o
);

	reg ff_r;

	always @(posedge clk_i) begin
		ff_r <= d_i;
	end


	assign q_o = ~ff_r & d_i;

endmodule
*/

/* Code of elevator_machine:
`timescale 1ns/1ps

module elevator_machine(
	input rst_i,
	input clk_i,
	input up_btn_i1,
	input up_btn_i2,
	input down_btn_i2,
	input down_btn_i3,

	output reg[3:0] cur_floor_o,
	output reg direction1_o,
	output reg direction2_o
);
	//States
	parameter FLOOR1 = 4'b0001;
	parameter FLOOR2 = 4'b0010;
	parameter FLOOR3 = 4'b0011;

	parameter MIDFLOOR2UP = 4'b0101;
	parameter MIDFLOOR2DOWN = 4'b0100;

	parameter TIMER_MAX = 15000;  // 2 seconds at 50MHz clock

	reg[3:0] currentstate, nextstate;
	reg [31:0] timer;  // 32-bit counter to track time
	reg timer_done;    // Flag to indicate when 2 seconds have passed
	reg oneloop;

        //state register
	always @(posedge clk_i) begin
		if(timer_done) begin
			currentstate <= nextstate;
			direction1_o <= 0;
			direction2_o <= 0;
		end
		else currentstate <= currentstate;
	end

	//Timer logic: 2second
	always @(posedge clk_i or posedge rst_i) begin
		begin
			if(timer_done == 0 && timer < TIMER_MAX) begin
				timer <= timer +1;
				timer_done <= 0;
			end
			else begin
				timer_done <= 1;
			end
		end
	end

	//next state logic
	always @(*) begin
		if(rst_i) begin
			currentstate <= FLOOR1;
			nextstate <= FLOOR1;
			timer <= 0;
			timer_done <= 1;
			direction1_o <= 0;
			direction2_o <= 0;
		end

		if(up_btn_i1 || up_btn_i2 || down_btn_i2 || down_btn_i3) begin
			timer <= 0;
			timer_done <= 0;
		end

		case (currentstate)
			FLOOR1: begin
				if(up_btn_i2 || down_btn_i2) nextstate = FLOOR2;
				if(down_btn_i3) begin
					nextstate = MIDFLOOR2UP;
					oneloop = 1;
				end
			end

			FLOOR2: begin
				if(up_btn_i1) nextstate = FLOOR1;
				if(down_btn_i3) nextstate = FLOOR3;
			end

			MIDFLOOR2UP: begin 
				if(oneloop == 1) begin
					nextstate = FLOOR3;
					timer_done = 0;
					timer = 0;
					oneloop = 0;
				end
			end

			MIDFLOOR2DOWN: begin
				if(oneloop == 1) begin
					nextstate = FLOOR1;
					timer_done = 0;
					timer = 0;
					oneloop = 0;
				end
			end

			FLOOR3: begin
				if(up_btn_i2 || down_btn_i2) nextstate = FLOOR2;
				if(up_btn_i1) begin
					nextstate = MIDFLOOR2DOWN;
					oneloop = 1;
				end
			end
		endcase
	end

	//output logic
	always@(*) begin
		if (currentstate == FLOOR1) begin
			cur_floor_o = FLOOR1;
			direction1_o = (nextstate == FLOOR2 || nextstate == MIDFLOOR2UP);
			direction2_o = 0;
		end
		else if (currentstate == FLOOR2) begin
			cur_floor_o = FLOOR2;
			direction1_o = (nextstate == FLOOR3);
			direction2_o = (nextstate == FLOOR1);
		end
		else if (currentstate == MIDFLOOR2UP) begin
			cur_floor_o = FLOOR2;
			direction1_o = 1;
			direction2_o = 0;
		end
		else if (currentstate == MIDFLOOR2DOWN) begin
			cur_floor_o = FLOOR2;
			direction1_o = 0;
			direction2_o = 1;
		end
		else if (currentstate == FLOOR3) begin
			cur_floor_o = FLOOR3;
			direction1_o = 0;
			direction2_o = (nextstate == FLOOR2 || nextstate == MIDFLOOR2DOWN);
		end
	end

endmodule
*/
