// Digital circuit 박건호_2023320123.dig as structural Verilog
module \박건호_2023320123  (
  input  Clock_In,
  input  in_2
);

  wire Down_button_2_out, Down_button_3_out, Down_button_4_out, Reset_out, u_elevator_machine_direction1_o,
       u_elevator_machine_direction2_o, Up_button_1_out, Up_button_2_out, Up_button_3_out;
  wire [3:0] u_elevator_machine_cur_floor_o;

  Button Reset (.out(Reset_out));
  Button Up_button_1 (.out(Up_button_1_out));
  Button Up_button_2 (.out(Up_button_2_out));
  Button Down_button_2 (.out(Down_button_2_out));
  Button Up_button_3 (.out(Up_button_3_out));
  Button Down_button_3 (.out(Down_button_3_out));
  Button Down_button_4 (.out(Down_button_4_out));
  elevator_machine #(.applicationType("IVERILOG")) u_elevator_machine (
    .rst_i(Reset_out), .clk_i(Clock_In), .up_btn_i1(Up_button_1_out), .up_btn_i2(Up_button_2_out),
    .up_btn_i3(Up_button_3_out), .down_btn_i2(Down_button_2_out), .down_btn_i3(Down_button_3_out),
    .down_btn_i4(Down_button_4_out), .cur_floor_o(u_elevator_machine_cur_floor_o),
    .direction1_o(u_elevator_machine_direction1_o), .direction2_o(u_elevator_machine_direction2_o));
  LED UP_led (.in(u_elevator_machine_direction1_o));
  LED DOWN_led (.in(u_elevator_machine_direction2_o));
  Seven_Seg_Hex seven_seg_hex_1 (.d(u_elevator_machine_cur_floor_o), .dp(in_2));

  // Notes on the sheet:
  //   Clock_In: Hz: 1000
endmodule

/* Code of elevator_machine:
`timescale 1ns/1ps

module elevator_machine(
	input rst_i,
	input clk_i,
	input up_btn_i1,
	input up_btn_i2,
	input up_btn_i3,
	input down_btn_i2,
	input down_btn_i3,
	input down_btn_i4,

	output reg[3:0] cur_floor_o,
	output reg direction1_o,
	output reg direction2_o
);
	//States
	parameter FLOOR1 = 4'b0001;
	parameter FLOOR2 = 4'b0010;
	parameter FLOOR3 = 4'b0011;
	parameter FLOOR4 = 4'b0100;

	parameter MIDFLOOR2UP1to3 = 4'b0101;
	parameter MIDFLOOR2DOWN3to1 = 4'b0110;

	parameter MIDFLOOR3UP2to4 = 4'b0111;
	parameter MIDFLOOR3DOWN4to2 = 4'b1000;

	parameter MIDFLOOR2UP1to4 = 4'b1001;
	parameter MIDFLOOR2DOWN4to1 = 4'b1010;

	parameter MIDFLOOR3UP1to4 = 4'b1011;
	parameter MIDFLOOR3DOWN4to1 = 4'b1100;

	parameter TIMER_MAX = 2000;  // 2 seconds at 1KHz clock

	reg[3:0] currentstate, nextstate;
	reg [31:0] timer;  // 32-bit counter to track time
	reg timer_done;    // Flag to indicate when 2 seconds have passed
	reg oneloop, oneloop2;

        //state register
	always @(posedge clk_i) begin
		if(timer_done) begin
			currentstate <= nextstate;
			direction1_o <= 0;
			direction2_o <= 0;
		end
		else currentstate <= currentstate;
	end

	//Timer logic: 2second
	always @(posedge clk_i or posedge rst_i) begin
		begin
			if(timer_done == 0 && timer < TIMER_MAX) begin
				timer <= timer +1;
				timer_done <= 0;
			end
			else begin
				timer_done <= 1;
			end
		end
	end

	//next state logic
	always @(*) begin
		if(rst_i) begin
			currentstate <= FLOOR1;
			nextstate <= FLOOR1;
			timer <= 0;
			timer_done <= 1;
			direction1_o <= 0;
			direction2_o <= 0;
		end

		if(up_btn_i1 || up_btn_i2 || up_btn_i3 || down_btn_i2 || down_btn_i3 || down_btn_i4) begin
			timer <= 0;
			timer_done <= 0;
		end

		case (currentstate)
			FLOOR1: begin
				if(up_btn_i2 || down_btn_i2) nextstate = FLOOR2;
				if(down_btn_i3 || up_btn_i3) begin
					nextstate = MIDFLOOR2UP1to3;
					oneloop = 1;
				end
				if(down_btn_i4) begin
					nextstate = MIDFLOOR2UP1to4;
					oneloop = 1;
					oneloop2 = 1;
				end
			end

			FLOOR2: begin
				if(up_btn_i1) nextstate = FLOOR1;
				if(down_btn_i3 || up_btn_i3) nextstate = FLOOR3;
				if(down_btn_i4) begin
					nextstate = MIDFLOOR3UP2to4;
					oneloop = 1;
				end
			end

			FLOOR3: begin
				if(down_btn_i4) nextstate = FLOOR4;
				if(up_btn_i2 || down_btn_i2) nextstate = FLOOR2;
				if(up_btn_i1) begin
					nextstate = MIDFLOOR2DOWN3to1;
					oneloop = 1;
				end
			end
		
			FLOOR4: begin
				if(down_btn_i3 || up_btn_i3) nextstate = FLOOR3;
				if(down_btn_i2 || up_btn_i2) begin
					nextstate = MIDFLOOR3DOWN4to2;
					oneloop = 1;
				end
				if(up_btn_i1) begin
					nextstate = MIDFLOOR3DOWN4to1;
					oneloop = 1;
					oneloop2 = 1;
				end
			end

			MIDFLOOR2UP1to3: begin 
				if(oneloop == 1) begin
					nextstate = FLOOR3;
					timer_done = 0;
					timer = 0;
					oneloop = 0;
				end
			end

			MIDFLOOR2DOWN3to1: begin
				if(oneloop == 1) begin
					nextstate = FLOOR1;
					timer_done = 0;
					timer = 0;
					oneloop = 0;
				end
			end

			MIDFLOOR3UP2to4: begin
				if(oneloop == 1) begin
					nextstate = FLOOR4;
					timer_done = 0;
					timer = 0;
					oneloop = 0;
				end
			end

			MIDFLOOR3DOWN4to2: begin
				if(oneloop == 1) begin
					nextstate = FLOOR2;
					timer_done = 0;
					timer = 0;
					oneloop = 0;
				end
			end

			MIDFLOOR2UP1to4: begin
				if(oneloop == 1) begin
					nextstate = MIDFLOOR3UP1to4;
					timer_done = 0;
					timer = 0;
					oneloop = 0;
				end
			end

			MIDFLOOR3UP1to4: begin
				if(oneloop2 == 1) begin
					nextstate = FLOOR4;
					timer_done = 0;
					timer = 0;
					oneloop2 = 0;
				end
			end

			MIDFLOOR3DOWN4to1: begin
				if(oneloop == 1) begin
					nextstate = MIDFLOOR2DOWN4to1;
					timer_done = 0;
					timer = 0;
					oneloop = 0;
				end
			end

			MIDFLOOR2DOWN4to1: begin
				if(oneloop2 == 1) begin
					nextstate = FLOOR1;
					timer_done = 0;
					timer = 0;
					oneloop2 = 0;
				end
			end
		endcase
	end

	//output logic
	always@(*) begin
		if (currentstate == FLOOR1) begin
			cur_floor_o = FLOOR1;
			direction1_o = (nextstate == FLOOR2 || nextstate == MIDFLOOR2UP1to3 || nextstate == MIDFLOOR2UP1to4);
			direction2_o = 0;
		end
		else if (currentstate == FLOOR2) begin
			cur_floor_o = FLOOR2;
			direction1_o = (nextstate == FLOOR3 || nextstate == MIDFLOOR3UP2to4);
			direction2_o = (nextstate == FLOOR1);
		end
		else if (currentstate == FLOOR3) begin
			cur_floor_o = FLOOR3;
			direction1_o = (nextstate == FLOOR4);
			direction2_o = (nextstate == FLOOR2 || nextstate == MIDFLOOR2DOWN3to1);
		end
		else if (currentstate == FLOOR4) begin
			cur_floor_o = FLOOR4;
			direction1_o = 0;
			direction2_o = (nextstate == FLOOR3 || nextstate == MIDFLOOR3DOWN4to2 || nextstate == MIDFLOOR3DOWN4to1);
		end
		else if (currentstate == MIDFLOOR2UP1to3 || currentstate == MIDFLOOR2UP1to4) begin
			cur_floor_o = FLOOR2;
			direction1_o = 1;
			direction2_o = 0;
		end
		else if (currentstate == MIDFLOOR2DOWN3to1 || currentstate == MIDFLOOR2DOWN4to1) begin
			cur_floor_o = FLOOR2;
			direction1_o = 0;
			direction2_o = 1;
		end
		else if (currentstate == MIDFLOOR3UP2to4 || currentstate == MIDFLOOR3UP1to4) begin
			cur_floor_o = FLOOR3;
			direction1_o = 1;
			direction2_o = 0;
		end
		else if (currentstate == MIDFLOOR3DOWN4to2 || currentstate == MIDFLOOR3DOWN4to1) begin
			cur_floor_o = FLOOR3;
			direction1_o = 0;
			direction2_o = 1;
		end
	end

endmodule
*/
