// Digital circuit test.dig as structural Verilog
module test (
  input  input1,
  input  input2,
  output \output 
);

  xor xor_1 (\output , input1, input2);
  xor_gate #(.applicationType("IVERILOG")) u_xor_gate ();  // open: A, B, Y
  LED led_1 (.in(\output ));
endmodule

/* Code of xor_gate:
module xor_gate {
	input wire A,
	input wire B,
	output wire Y
};

assign Y = A ^ B;

endmodule
*/
