// Digital circuit vending.dig as structural Verilog
module vending (
  input  Clock_In
);

  wire _100_won_out, _500_won_out, _1000_won_out, Reset_out, u_coffee_vending_machine_coffee_o,
       u_edge_detector_2_q_o, u_edge_detector_3_q_o, u_edge_detector_q_o, u_synchronizer_2_q_o,
       u_synchronizer_3_q_o, u_synchronizer_q_o;
  wire [3:0] u_coffee_vending_machine_acc_coin1_o, u_coffee_vending_machine_acc_coin2_o,
       u_coffee_vending_machine_change_o;

  Button _100_won (.out(_100_won_out));
  Button _500_won (.out(_500_won_out));
  Button _1000_won (.out(_1000_won_out));
  synchronizer #(.applicationType("IVERILOG")) u_synchronizer (
    .clk_i(Clock_In), .d_i(_100_won_out), .q_o(u_synchronizer_q_o));
  synchronizer #(.applicationType("IVERILOG")) u_synchronizer_2 (
    .clk_i(Clock_In), .d_i(_500_won_out), .q_o(u_synchronizer_2_q_o));
  synchronizer #(.applicationType("IVERILOG")) u_synchronizer_3 (
    .clk_i(Clock_In), .d_i(_1000_won_out), .q_o(u_synchronizer_3_q_o));
  edge_detector #(.applicationType("IVERILOG")) u_edge_detector (
    .clk_i(Clock_In), .d_i(u_synchronizer_q_o), .q_o(u_edge_detector_q_o));
  edge_detector #(.applicationType("IVERILOG")) u_edge_detector_2 (
    .clk_i(Clock_In), .d_i(u_synchronizer_2_q_o), .q_o(u_edge_detector_2_q_o));
  edge_detector #(.applicationType("IVERILOG")) u_edge_detector_3 (
    .clk_i(Clock_In), .d_i(u_synchronizer_3_q_o), .q_o(u_edge_detector_3_q_o));
  Button Reset (.out(Reset_out));
  coffee_vending_machine #(.applicationType("IVERILOG")) u_coffee_vending_machine (
    .rst_i(Reset_out), .clk_i(Clock_In), .in_100_i(u_edge_detector_q_o), .in_500_i(u_edge_detector_2_q_o),
    .in_1000_i(u_edge_detector_3_q_o), .coffee_o(u_coffee_vending_machine_coffee_o),
    .acc_coin1_o(u_coffee_vending_machine_acc_coin1_o), .acc_coin2_o(u_coffee_vending_machine_acc_coin2_o),
    .change_o(u_coffee_vending_machine_change_o));
  LED Coffee_Out (.in(u_coffee_vending_machine_coffee_o));
  Seven_Seg_Hex seven_seg_hex_1 (.d(u_coffee_vending_machine_acc_coin2_o), .dp(1'b0));
  Seven_Seg_Hex seven_seg_hex_2 (.d(u_coffee_vending_machine_acc_coin1_o), .dp(1'b0));
  Seven_Seg_Hex seven_seg_hex_3 (.d(u_coffee_vending_machine_change_o), .dp(1'b0));

  // Notes on the sheet:
  //   Clock_In: Hz: 2147483647
endmodule

/* Code of synchronizer:
`timescale 1ns/1ps

module synchronizer (
	 input clk_i
	,input d_i

	,output reg q_o
);


	reg ff1_r;

	always @(posedge clk_i) begin
		ff1_r <= d_i;
		q_o <= ff1_r;
	end

endmodule
*/

/* Code of edge_detector:
`timescale 1ns/1ps

module edge_detector (
	 input clk_i
	,input d_i

	,output q_o
);

	reg ff_r;

	always @(posedge clk_i) begin
		ff_r <= d_i;
	end


	assign q_o = ~ff_r & d_i;

endmodule
*/

/* Code of coffee_vending_machine:
`timescale 1ns/1ps

module coffee_vending_machine(
	 input rst_i
	,input clk_i
	,input in_100_i
	,input in_500_i
	,input in_1000_i

	,output reg coffee_o
	,output reg [3:0] acc_coin1_o
	,output reg [3:0] acc_coin2_o
	,output reg [3:0] change_o
);

	// States
	parameter COUNTING = 1'b0;
	parameter DISPENSE = 1'b1;

	reg currentstate, nextstate;

	// state register
	always @(posedge clk_i) begin
		if (rst_i) currentstate <= COUNTING; 
		else currentstate <= nextstate;
	end

	// next state logic
	always @(*) begin
		case (currentstate)
			COUNTING: if (acc_coin_r >= 6) nextstate = DISPENSE;
			             else nextstate = currentstate;
			DISPENSE: if (rst_i | in_100_i | in_500_i | in_1000_i) nextstate = COUNTING;
			             else nextstate = currentstate;
			default: nextstate = currentstate; 	// This line is not neccessary
		endcase
	end

	reg [3:0] acc_coin_r;
	// acc_coin_r
	always @(posedge clk_i) begin
	   	if (rst_i) acc_coin_r <= 0;
		else if (currentstate == COUNTING) begin
			if (in_100_i) acc_coin_r <= acc_coin_r + 1;
			else if (in_500_i) acc_coin_r <= acc_coin_r + 5;
			else if (in_1000_i) acc_coin_r	<= acc_coin_r + 10;
		end
		else begin
		  	if (in_100_i) acc_coin_r <= 1;
			else if (in_500_i) acc_coin_r <= 5;
			else if (in_1000_i) acc_coin_r	<= 10;
		end
	end

	// ouput logic
	always @(*) begin
		if (currentstate == DISPENSE) begin
			coffee_o = 1'b1;
			change_o = acc_coin_r - 6;
		end
		else begin
			coffee_o = 1'b0;
			change_o = 0;
		end
	end

	always @(*) begin
		if (acc_coin_r == 10) begin
			acc_coin1_o = 1;
			acc_coin2_o = 0;
		end
		else begin
			acc_coin1_o = 0;
			acc_coin2_o = acc_coin_r;
		end
	end

endmodule
*/
